# Fritzing sketch lomba (saved by Fritzing 0.9.3b)

parts:
  BATT1 = LiPoly Battery (1300mAh)
  ESP32_DEV_KIT1 = MH-ET LIVE ESP32 DEVKIT 38 pins
  LORA_SX1279 = Osoyoo SX1278-ra-02
  OLED_I2C1 = OLED 128x64 I2C Monochrome Display
  D1 = Rectifier Diode [part_number=1N4001 package="300 mil [THT]"]
  U1 = Voltage Regulator - 5V [package="TO220 [THT]"]

nets:
  N1: BATT1.positive, U1.input_voltage
  N2: BATT1.negative, U1.GND
  N3: ESP32_DEV_KIT1.3V3, ESP32_DEV_KIT1.RST
  N4: ESP32_DEV_KIT1.IO27, ESP32_DEV_KIT1.IO14, LORA_SX1279.RST
  N5: ESP32_DEV_KIT1.IO12, ESP32_DEV_KIT1.GND#58
  N6: ESP32_DEV_KIT1.IO23, LORA_SX1279.MOSI
  N7: ESP32_DEV_KIT1.IO22, ESP32_DEV_KIT1.TXD0, OLED_I2C1.SCK
  N8: ESP32_DEV_KIT1.IO21, OLED_I2C1.SDA
  N9: ESP32_DEV_KIT1.GND#70, ESP32_DEV_KIT1.IO19, LORA_SX1279.MISO
  N10: ESP32_DEV_KIT1.IO18, LORA_SX1279.SCK
  N11: ESP32_DEV_KIT1.IO5, ESP32_DEV_KIT1.IO17, LORA_SX1279.NSS
  N12: D1.anode, U1.output_voltage

custom parts:
  LiPoly Battery (1300mAh): Lithium Ion Polymer Battery (1300mAh)
  MH-ET LIVE ESP32 DEVKIT 38 pins: http://mh.nodebb.com/topic/2/mh-et-live-esp32-devkit
  Osoyoo SX1278-ra-02: Osoyoo Long Distance wireless transceiver Uart LoRa Module.
