# Fritzing sketch lomba_robot (saved by Fritzing 0.9.3b)

parts:
  DHT2 = DHT22 Humidity and Temperature Sensor
  M7 = DC Motor
  M8 = DC Motor
  ESP32_-_Back2 = ESP32 - CAM
  Part1 = MQ-4
  Part2 = MQ-7 breakout
  BATT1 = LiPoly Battery (1300mAh)
  S1 = H-Bridge with L298N
  ESP32_DEV_KIT1 = MH-ET LIVE ESP32 DEVKIT 38 pins
  LORA_SX1279 = Osoyoo SX1278-ra-02
  D1 = Rectifier Diode [part_number=1N4001 package="300 mil [THT]"]
  U1 = Voltage Regulator - 5V [package="TO220 [THT]"]

nets:
  N1: DHT2.DATA, ESP32_DEV_KIT1.IO13
  N2: M7.pin_1, S1.M2-02
  N3: M7.pin_2, S1.M2-01
  N4: M8.pin_1, S1.M1-02
  N5: M8.pin_2, S1.M1-01
  N6: ESP32_-_Back2.GPIO14, S1.IN1
  N7: ESP32_-_Back2.GPIO15, S1.IN2
  N8: ESP32_-_Back2.GPIO13, S1.IN3
  N9: ESP32_-_Back2.GPIO12, S1.IN4
  N10: ESP32_-_Back2.5V, D1.cathode
  N11: Part1.AO, ESP32_DEV_KIT1.IO35, ESP32_DEV_KIT1.IO32
  N12: Part2.AO, ESP32_DEV_KIT1.IO34
  N13: BATT1.positive, U1.input_voltage
  N14: BATT1.negative, U1.GND
  N15: S1.ENA, S1.ENA-5V
  N16: S1.ENB, S1.ENB-5V
  N17: ESP32_DEV_KIT1.IO14, ESP32_DEV_KIT1.IO12, LORA_SX1279.RST
  N18: ESP32_DEV_KIT1.IO23, LORA_SX1279.MOSI
  N19: ESP32_DEV_KIT1.IO19, LORA_SX1279.MISO
  N20: ESP32_DEV_KIT1.IO18, LORA_SX1279.SCK
  N21: ESP32_DEV_KIT1.IO5, LORA_SX1279.NSS
  N22: D1.anode, U1.output_voltage

custom parts:
  ESP32 - CAM: The ESP32-CAM has a very competitive small-size camera module that can operate independently as a minimum system with a footprint of only 27*40.5*4.5mm and a deep sleep current of up to 6mA.
  MQ-7 breakout: SKU: 101282
  LiPoly Battery (1300mAh): Lithium Ion Polymer Battery (1300mAh)
  H-Bridge with L298N: h-bridge
  MH-ET LIVE ESP32 DEVKIT 38 pins: http://mh.nodebb.com/topic/2/mh-et-live-esp32-devkit
  Osoyoo SX1278-ra-02: Osoyoo Long Distance wireless transceiver Uart LoRa Module.
